// Logisim project mycirc.circ as structural Verilog: 3 circuits, main circuit MUX2x1
module MUX4x1 (
  input  in0,
  input  in1,
  input  in2,
  input  in3,
  input  sel0,
  input  sel1,
  output mux_out
);

  wire mux2x1_1_mux_out, mux2x1_2_mux_out;

  MUX2x1 mux2x1_1 (.in0(in0), .in1(in1), .Sel(sel0), .mux_out(mux2x1_1_mux_out));
  MUX2x1 mux2x1_2 (.in0(in2), .in1(in3), .Sel(sel0), .mux_out(mux2x1_2_mux_out));
  MUX2x1 mux2x1_3 (.in0(mux2x1_1_mux_out), .in1(mux2x1_2_mux_out), .Sel(sel1), .mux_out(mux_out));
endmodule

module MUX2x1 (
  input  in0,
  input  in1,
  input  Sel,
  output mux_out
);

  wire and_1_out, and_2_out, not_1_out;

  not not_1 (not_1_out, Sel);
  and and_1 (and_1_out, in0, not_1_out);
  and and_2 (and_2_out, in1, Sel);
  or or_1 (mux_out, and_1_out, and_2_out);
endmodule

module main (
  input  write,
  input  [31:0] instruction
);

  wire clk_out;
  wire [31:0] adder_1_out, PC_q;

  Register #(.width(32)) PC (.D(adder_1_out), .en(write), .clk(clk_out), .Q(PC_q), .clr(PC_q[26]));
  Clock clk (.out(clk_out));
  ROM #(.addrWidth(24), .dataWidth(32)) InstructionMemory (.addr(PC_q[25:2]), .data(instruction));
  Adder #(.width(32)) adder_1 (.a(PC_q), .b(32'h4), .out(adder_1_out), .cin(1'b0));  // open: cout
endmodule
